# Fritzing sketch Argus Vac (saved by Fritzing 1.0.5)

parts:
  Part1 = Arduino Mega 2560 (Rev3)
  Mod1 = Raspberry Pi 4B  # not connected
  M2 = Stepper Motor - Bipolar
  BAT1 = Lithium Ion Polymer Battery 11.1v 5000mah
  C2 = Electrolytic Capacitor [capacitance=100µF voltage=35V package="200 mil [THT, electrolytic]"]
  Left_Motor_Driver = Pololu A4988 [package=SO16]
  Right_Motor_Driver = Pololu A4988 [package=SO16]
  M3 = RioRand LM2596
  M4 = Stepper Motor - Bipolar
  C3 = Electrolytic Capacitor [capacitance=100µF voltage=35V package="200 mil [THT, electrolytic]"]
  J3 = Wago 221-415
  J4 = Wago 221-415
  F1 = FUSE [package=fuse_5mm]
  M5 = DC Mini Metal Gear Motor
  M6 = DC Mini Metal Gear Motor
  J5 = Wago 221-415
  J6 = Wago 221-415
  J7 = Wago 221-413
  J8 = Wago 221-413
  M7 = DC Motor [voltage_(max)=6V voltage_(min)=3V]
  A1 = drv-1012
  J9 = Wago 221-413
  J10 = Wago 221-413
  C4 = Electrolytic Capacitor [capacitance=0.1µF voltage=50V package="100 mil [THT, electrolytic]"]
  C5 = Electrolytic Capacitor [capacitance=0.1µF voltage=50V package="100 mil [THT, electrolytic]"]
  L298N1 = L298N DC motor driver

nets:
  N1: Part1.D13_PWM, L298N1.ENA
  N2: Part1.D12_PWM, L298N1.ENB
  N3: Part1.D9_PWM, A1.Pin_4
  N4: Part1.D8_PWM, A1.Pin_8
  VDD: Part1.5V, Left_Motor_Driver.VDD, Right_Motor_Driver.VDD, A1.Pin_5, A1.Pin_7, J9.Pin_1, J9.Pin_2, J9.Pin_3
  N5: Part1.GND, Left_Motor_Driver.GND#8, Right_Motor_Driver.GND#8, M3.Pin_4, J7.Pin_1, J7.Pin_2, J7.Pin_3, A1.Pin_1, A1.Pin_3, J10.Pin_1, J10.Pin_2, J10.Pin_3
  VIN: Part1.VIN, M3.Pin_3, J8.Pin_1, J8.Pin_2, J8.Pin_3, L298N1.5V
  N6: Part1.D2_PWM, Left_Motor_Driver.STEP
  N7: Part1.D3_PWM, Left_Motor_Driver.DIR
  N8: Part1.D4_PWM, Right_Motor_Driver.STEP
  N9: Part1.D5_PWM, Right_Motor_Driver.DIR
  N10: Part1.D46, L298N1.IN3
  N11: Part1.D48, L298N1.IN4
  N12: Part1.D50, L298N1.IN2
  N13: Part1.D52, L298N1.IN1
  N14: M2.A, Left_Motor_Driver.1A
  N15: M2.C, Left_Motor_Driver.1B
  N16: M2.B, Left_Motor_Driver.2A
  N17: M2.D, Left_Motor_Driver.2B
  N18: BAT1.positive, F1.1
  12V: BAT1.negative, C2.-, Left_Motor_Driver.GND#14, Right_Motor_Driver.GND#14, Right_Motor_Driver.VMOT, M3.Pin_1, M3.Pin_2, C3.-, C3.+, J3.Pin_1, J3.Pin_2, J3.Pin_3, J3.Pin_4, J3.Pin_5, J4.Pin_1, J4.Pin_2, J4.Pin_3, J4.Pin_4, J4.Pin_5, F1.2, J5.Pin_1, J5.Pin_3, J5.Pin_4, J5.Pin_5, J6.Pin_1, J6.Pin_2, J6.Pin_3, A1.Pin_11, A1.Pin_12, L298N1.12V, L298N1.GND
  N19: C2.+, Left_Motor_Driver.VMOT
  N20: Left_Motor_Driver.RESET, Left_Motor_Driver.SLEEP
  N21: Right_Motor_Driver.RESET, Right_Motor_Driver.SLEEP
  N22: Right_Motor_Driver.1B, M4.C
  N23: Right_Motor_Driver.1A, M4.A
  N24: Right_Motor_Driver.2A, M4.B
  N25: Right_Motor_Driver.2B, M4.D
  N26: M5.IN1, C5.+, L298N1.OUT4
  N27: M5.IN2, C5.-, L298N1.OUT3
  N28: M6.IN1, C4.+, L298N1.OUT1
  N29: M6.IN2, C4.-, L298N1.OUT2
  N30: M7.pin_1, A1.Pin_9
  N31: M7.pin_2, A1.Pin_10

custom parts:
  Wago 221-415: Wago 221-415 5 position splicing connector 12AWG.
  Wago 221-413: Wago 221-413 3 position splicing connector 12AWG.
  drv-1012: .The BTS7960 is a fully integrated high current H bridge module for motor drive applications.
  L298N DC motor driver: 2x DC motor driver with 78M05 positive voltage regulator (7..35 V) L298N: max 46 V, 2 A Set 5 V Enable jumper to enable 5 V regultor (needed for the L298N) and +5 V output at screw terminal or supply external +5 V at screw terminal Set ENA and/or ENB to +5 V to enable motor permanently or supply ENA and/or ENB with PWM signal IN1 and IN2 set rotation directory for motor A (OUT1/OUT2) IN2 and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

// code stored in the sketch: test_code_nema.ino
/*
  Argus Vac - Drive Motor Control
  ---------------------------------------------------------------------------
  Hardware (from the Fritzing wiring audit):

    Arduino Mega 2560          Left A4988 driver      Left stepper (M2)
      D2  ---------------------> STEP
      D3  ---------------------> DIR
      5V  ---------------------> VDD (logic power)
      GND ---------------------> GND (logic ground)
                                 1A/1B/2A/2B  --------> A / C / B / D

    Arduino Mega 2560          Right A4988 driver     Right stepper (M4)
      D4  ---------------------> STEP
      D5  ---------------------> DIR
      5V  ---------------------> VDD (logic power)
      GND ---------------------> GND (logic ground)
                                 1A/1B/2A/2B  --------> A / C / B / D

    LiPo (11.1V) -> LM2596 buck converter -> Arduino VIN
    LiPo (+)     -> VMOT on both A4988 drivers (motor power)
    LiPo (-)     -> GND(motor) on both A4988 drivers, and driver GND(logic)
                    is tied to Arduino GND (common ground - required!)

  Both drivers have RESET tied to SLEEP (required for the A4988 to run).
  ENABLE, MS1, MS2, MS3 are left unconnected on purpose -> the Pololu A4988
  carrier pulls ENABLE low (driver enabled) and MS1-3 low (full-step mode)
  by default, so this is a valid, simple configuration.

  IMPORTANT - fix these 3 wiring bugs found in the .fzz before you power this up:
    1. C2's "-" leg is floating -> connect it to the battery/GND rail.
    2. C3's "+" leg is floating -> connect it to the battery/VMOT (+) rail.
    3. The RIGHT driver's motor-side GND pin (next to VMOT) isn't wired to
       anything -> connect it to the battery negative rail, same as the
       left driver. Running it without this is unreliable/unsafe for the
       driver.

  Library required: AccelStepper (Arduino Library Manager -> "AccelStepper" by Mike McCauley)
*/

#include <AccelStepper.h>

// ---- Pin assignments (matches the wiring above) ----------------------------
const uint8_t LEFT_STEP_PIN  = 2;
const uint8_t LEFT_DIR_PIN   = 3;
const uint8_t RIGHT_STEP_PIN = 4;
const uint8_t RIGHT_DIR_PIN  = 5;

// ---- Tuning ------------------------------------------------------------
const float MAX_SPEED_SPS     = 800.0;  // steps/sec ceiling
const float ACCEL_SPS2        = 600.0;  // steps/sec^2
const float CRUISE_SPEED_SPS  = 500.0;  // normal driving speed
const float TURN_SPEED_SPS    = 350.0;  // speed used while turning in place

// AccelStepper::DRIVER mode = 2 pins (STEP, DIR), which is exactly what an
// A4988 needs.
AccelStepper leftMotor(AccelStepper::DRIVER, LEFT_STEP_PIN, LEFT_DIR_PIN);
AccelStepper rightMotor(AccelStepper::DRIVER, RIGHT_STEP_PIN, RIGHT_DIR_PIN);

void setup() {
  leftMotor.setMaxSpeed(MAX_SPEED_SPS);
  leftMotor.setAcceleration(ACCEL_SPS2);

  rightMotor.setMaxSpeed(MAX_SPEED_SPS);
  rightMotor.setAcceleration(ACCEL_SPS2);

  stopMotors();
}

void loop() {
  // Simple demo pattern - replace with your own navigation/vacuum logic.
  driveForward(CRUISE_SPEED_SPS);
  runFor(2000);   // 2 seconds forward

  stopMotors();
  runFor(300);

  turnRight(TURN_SPEED_SPS);
  runFor(650);    // roughly a 90 degree pivot - tune this for your gearing

  stopMotors();
  runFor(300);
}

// ---- Motion primitives ---------------------------------------------------
// NOTE: if the robot drives backward when you ask for forward (or turns the
// wrong way), swap the sign on that motor's speed below rather than
// re-wiring anything - it's just a matter of which coil pair got called A/C.

void driveForward(float speed) {
  leftMotor.setSpeed(speed);
  rightMotor.setSpeed(speed);
}

void driveBackward(float speed) {
  leftMotor.setSpeed(-speed);
  rightMotor.setSpeed(-speed);
}

void turnLeft(float speed) {
  // Left wheel back, right wheel forward = pivot left in place.
  leftMotor.setSpeed(-speed);
  rightMotor.setSpeed(speed);
}

void turnRight(float speed) {
  leftMotor.setSpeed(speed);
  rightMotor.setSpeed(-speed);
}

void stopMotors() {
  leftMotor.setSpeed(0);
  rightMotor.setSpeed(0);
}

// Runs the motors at whatever speed was last set, for the given duration.
void runFor(unsigned long ms) {
  unsigned long start = millis();
  while (millis() - start < ms) {
    leftMotor.runSpeed();
    rightMotor.runSpeed();
  }
}
