# Fritzing sketch Argus Vac Final (saved by Fritzing 1.0.5)

parts:
  Arduino_mega = Arduino Mega 2560 (Rev3)
  OrangePi_5(Raspberry_Pi_image_as_substitute) = Raspberry Pi 4B  # not connected
  Left_Wheel_Motor = Stepper Motor - Bipolar
  5000_Mah_11_1V_30C_3s_Lipo = Lithium Ion Polymer Battery 11.1v 5000mah
  C2 = Electrolytic Capacitor [capacitance=100µF voltage=35V package="200 mil [THT, electrolytic]"]
  Left_Motor_Driver = Pololu A4988 [package=SO16]
  Right_Motor_Driver = Pololu A4988 [package=SO16]
  12V_->_5V_DC-DC_Buck_Converter = RioRand LM2596
  Right_Wheel_Motor = Stepper Motor - Bipolar
  C3 = Electrolytic Capacitor [capacitance=100µF voltage=35V package="200 mil [THT, electrolytic]"]
  12V_Positive_Wago_1 = Wago 221-415
  12V_Negative_Wago_1 = Wago 221-415
  12AWG_10AMP_Fuse = FUSE [package=fuse_5mm]
  Frontish_Brush_Motor = DC Mini Metal Gear Motor
  Backish_brush_Motor = DC Mini Metal Gear Motor
  12V_Negative_Wago_2 = Wago 221-415
  12V_Positive_Wago_2 = Wago 221-415
  5V_Negative_Wago_1 = Wago 221-413
  5V_Positive_Wago_1 = Wago 221-413
  San_Ace_40_Axial_Fan = DC Motor [voltage_(max)=6V voltage_(min)=3V]
  San_Ace_40_Motor_Driver = drv-1012
  5V_Positive_Wago_2 = Wago 221-413
  5V_Negative_Wago_2 = Wago 221-413
  C4 = Electrolytic Capacitor [capacitance=0.1µF voltage=50V package="100 mil [THT, electrolytic]"]
  C5 = Electrolytic Capacitor [capacitance=0.1µF voltage=50V package="100 mil [THT, electrolytic]"]
  L298N1 = L298N DC motor driver
  S1 = SWITCH-DPDT [package=ayz0202]

nets:
  N1: Arduino_mega.GND, Left_Motor_Driver.GND#8, Right_Motor_Driver.GND#8, 12V_->_5V_DC-DC_Buck_Converter.Pin_4, 5V_Negative_Wago_1.Pin_1, 5V_Negative_Wago_1.Pin_2, 5V_Negative_Wago_1.Pin_3, San_Ace_40_Motor_Driver.Pin_1, San_Ace_40_Motor_Driver.Pin_3, 5V_Negative_Wago_2.Pin_1, 5V_Negative_Wago_2.Pin_2, 5V_Negative_Wago_2.Pin_3
  N2: Arduino_mega.D13_PWM, L298N1.ENA
  N3: Arduino_mega.D12_PWM, L298N1.ENB
  N4: Arduino_mega.D9_PWM, San_Ace_40_Motor_Driver.Pin_4
  N5: Arduino_mega.D8_PWM, San_Ace_40_Motor_Driver.Pin_8
  VDD: Arduino_mega.5V, Left_Motor_Driver.VDD, Right_Motor_Driver.VDD, San_Ace_40_Motor_Driver.Pin_5, San_Ace_40_Motor_Driver.Pin_7, 5V_Positive_Wago_2.Pin_1, 5V_Positive_Wago_2.Pin_2, 5V_Positive_Wago_2.Pin_3
  VIN: Arduino_mega.VIN, 12V_->_5V_DC-DC_Buck_Converter.Pin_3, 5V_Positive_Wago_1.Pin_1, 5V_Positive_Wago_1.Pin_2, 5V_Positive_Wago_1.Pin_3, L298N1.5V
  N6: Arduino_mega.D3_PWM, Left_Motor_Driver.DIR
  N7: Arduino_mega.D4_PWM, Left_Motor_Driver.STEP
  N8: Arduino_mega.D5_PWM, Right_Motor_Driver.DIR
  N9: Arduino_mega.D6_PWM, Right_Motor_Driver.STEP
  N10: Arduino_mega.D46, L298N1.IN3
  N11: Arduino_mega.D48, L298N1.IN4
  N12: Arduino_mega.D50, L298N1.IN2
  N13: Arduino_mega.D52, L298N1.IN1
  N14: Left_Wheel_Motor.A, Left_Motor_Driver.1A
  N15: Left_Wheel_Motor.C, Left_Motor_Driver.1B
  N16: Left_Wheel_Motor.B, Left_Motor_Driver.2A
  N17: Left_Wheel_Motor.D, Left_Motor_Driver.2B
  N18: 5000_Mah_11_1V_30C_3s_Lipo.positive, S1.5
  N19: 5000_Mah_11_1V_30C_3s_Lipo.negative, C2.-, Left_Motor_Driver.GND#14, Right_Motor_Driver.GND#14, 12V_->_5V_DC-DC_Buck_Converter.Pin_2, C3.-, 12V_Negative_Wago_1.Pin_1, 12V_Negative_Wago_1.Pin_2, 12V_Negative_Wago_1.Pin_3, 12V_Negative_Wago_1.Pin_4, 12V_Negative_Wago_1.Pin_5, 12V_Negative_Wago_2.Pin_1, 12V_Negative_Wago_2.Pin_3, 12V_Negative_Wago_2.Pin_4, 12V_Negative_Wago_2.Pin_5, San_Ace_40_Motor_Driver.Pin_11, L298N1.GND
  N20: C2.+, Left_Motor_Driver.VMOT, Right_Motor_Driver.VMOT, 12V_->_5V_DC-DC_Buck_Converter.Pin_1, C3.+, 12V_Positive_Wago_1.Pin_1, 12V_Positive_Wago_1.Pin_2, 12V_Positive_Wago_1.Pin_3, 12V_Positive_Wago_1.Pin_4, 12V_Positive_Wago_1.Pin_5, 12AWG_10AMP_Fuse.2, 12V_Positive_Wago_2.Pin_1, 12V_Positive_Wago_2.Pin_2, 12V_Positive_Wago_2.Pin_3, San_Ace_40_Motor_Driver.Pin_12, L298N1.12V
  N21: Left_Motor_Driver.RESET, Left_Motor_Driver.SLEEP
  N22: Right_Motor_Driver.RESET, Right_Motor_Driver.SLEEP
  N23: Right_Motor_Driver.1B, Right_Wheel_Motor.C
  N24: Right_Motor_Driver.1A, Right_Wheel_Motor.A
  N25: Right_Motor_Driver.2A, Right_Wheel_Motor.B
  N26: Right_Motor_Driver.2B, Right_Wheel_Motor.D
  N27: 12AWG_10AMP_Fuse.1, S1.4
  N28: Frontish_Brush_Motor.IN1, C5.+, L298N1.OUT4
  N29: Frontish_Brush_Motor.IN2, C5.-, L298N1.OUT3
  N30: Backish_brush_Motor.IN1, C4.+, L298N1.OUT1
  N31: Backish_brush_Motor.IN2, C4.-, L298N1.OUT2
  N32: San_Ace_40_Axial_Fan.pin_1, San_Ace_40_Motor_Driver.Pin_9
  N33: San_Ace_40_Axial_Fan.pin_2, San_Ace_40_Motor_Driver.Pin_10

custom parts:
  Wago 221-415: Wago 221-415 5 position splicing connector 12AWG.
  Wago 221-413: Wago 221-413 3 position splicing connector 12AWG.
  drv-1012: .The BTS7960 is a fully integrated high current H bridge module for motor drive applications.
  L298N DC motor driver: 2x DC motor driver with 78M05 positive voltage regulator (7..35 V) L298N: max 46 V, 2 A Set 5 V Enable jumper to enable 5 V regultor (needed for the L298N) and +5 V output at screw terminal or supply external +5 V at screw terminal Set ENA and/or ENB to +5 V to enable motor permanently or supply ENA and/or ENB with PWM signal IN1 and IN2 set rotation directory for motor A (OUT1/OUT2) IN2 and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

// code stored in the sketch: test_code_nema.ino
/*
  Argus Vac - Drive Motor Control
  ---------------------------------------------------------------------------
  Hardware (from the Fritzing wiring audit):

    Arduino Mega 2560          Left A4988 driver      Left stepper (M2)
      D2  ---------------------> STEP
      D3  ---------------------> DIR
      5V  ---------------------> VDD (logic power)
      GND ---------------------> GND (logic ground)
                                 1A/1B/2A/2B  --------> A / C / B / D

    Arduino Mega 2560          Right A4988 driver     Right stepper (M4)
      D4  ---------------------> STEP
      D5  ---------------------> DIR
      5V  ---------------------> VDD (logic power)
      GND ---------------------> GND (logic ground)
                                 1A/1B/2A/2B  --------> A / C / B / D

    LiPo (11.1V) -> LM2596 buck converter -> Arduino VIN
    LiPo (+)     -> VMOT on both A4988 drivers (motor power)
    LiPo (-)     -> GND(motor) on both A4988 drivers, and driver GND(logic)
                    is tied to Arduino GND (common ground - required!)

  Both drivers have RESET tied to SLEEP (required for the A4988 to run).
  ENABLE, MS1, MS2, MS3 are left unconnected on purpose -> the Pololu A4988
  carrier pulls ENABLE low (driver enabled) and MS1-3 low (full-step mode)
  by default, so this is a valid, simple configuration.

  IMPORTANT - fix these 3 wiring bugs found in the .fzz before you power this up:
    1. C2's "-" leg is floating -> connect it to the battery/GND rail.
    2. C3's "+" leg is floating -> connect it to the battery/VMOT (+) rail.
    3. The RIGHT driver's motor-side GND pin (next to VMOT) isn't wired to
       anything -> connect it to the battery negative rail, same as the
       left driver. Running it without this is unreliable/unsafe for the
       driver.

  Library required: AccelStepper (Arduino Library Manager -> "AccelStepper" by Mike McCauley)
*/

#include <AccelStepper.h>

// ---- Pin assignments (matches the wiring above) ----------------------------
const uint8_t LEFT_STEP_PIN  = 2;
const uint8_t LEFT_DIR_PIN   = 3;
const uint8_t RIGHT_STEP_PIN = 4;
const uint8_t RIGHT_DIR_PIN  = 5;

// ---- Tuning ------------------------------------------------------------
const float MAX_SPEED_SPS     = 800.0;  // steps/sec ceiling
const float ACCEL_SPS2        = 600.0;  // steps/sec^2
const float CRUISE_SPEED_SPS  = 500.0;  // normal driving speed
const float TURN_SPEED_SPS    = 350.0;  // speed used while turning in place

// AccelStepper::DRIVER mode = 2 pins (STEP, DIR), which is exactly what an
// A4988 needs.
AccelStepper leftMotor(AccelStepper::DRIVER, LEFT_STEP_PIN, LEFT_DIR_PIN);
AccelStepper rightMotor(AccelStepper::DRIVER, RIGHT_STEP_PIN, RIGHT_DIR_PIN);

void setup() {
  leftMotor.setMaxSpeed(MAX_SPEED_SPS);
  leftMotor.setAcceleration(ACCEL_SPS2);

  rightMotor.setMaxSpeed(MAX_SPEED_SPS);
  rightMotor.setAcceleration(ACCEL_SPS2);

  stopMotors();
}

void loop() {
  // Simple demo pattern - replace with your own navigation/vacuum logic.
  driveForward(CRUISE_SPEED_SPS);
  runFor(2000);   // 2 seconds forward

  stopMotors();
  runFor(300);

  turnRight(TURN_SPEED_SPS);
  runFor(650);    // roughly a 90 degree pivot - tune this for your gearing

  stopMotors();
  runFor(300);
}

// ---- Motion primitives ---------------------------------------------------
// NOTE: if the robot drives backward when you ask for forward (or turns the
// wrong way), swap the sign on that motor's speed below rather than
// re-wiring anything - it's just a matter of which coil pair got called A/C.

void driveForward(float speed) {
  leftMotor.setSpeed(speed);
  rightMotor.setSpeed(speed);
}

void driveBackward(float speed) {
  leftMotor.setSpeed(-speed);
  rightMotor.setSpeed(-speed);
}

void turnLeft(float speed) {
  // Left wheel back, right wheel forward = pivot left in place.
  leftMotor.setSpeed(-speed);
  rightMotor.setSpeed(speed);
}

void turnRight(float speed) {
  leftMotor.setSpeed(speed);
  rightMotor.setSpeed(-speed);
}

void stopMotors() {
  leftMotor.setSpeed(0);
  rightMotor.setSpeed(0);
}

// Runs the motors at whatever speed was last set, for the given duration.
void runFor(unsigned long ms) {
  unsigned long start = millis();
  while (millis() - start < ms) {
    leftMotor.runSpeed();
    rightMotor.runSpeed();
  }
}
